# Fritzing sketch pinout (saved by Fritzing 0.9.10b)
breadboards: 2

parts:
  Arduino_Uno = Arduino Uno (Rev3) - ICSP
  C1 = Electrolytic Capacitor [capacitance=100µF voltage=35V package="200 mil [THT, electrolytic]"]
  DRV_1 = DRV 8825 Stepper Motor Carrier, High Current [part_number="DRV 8825"]
  M2 = Stepper Motor - Bipolar
  RED = smd LED [color="Red (633nm)" package="1206 [SMD]"]
  GREEN = smd LED [color="Green (555nm)" package="1206 [SMD]"]
  S1 = Pushbutton [package="[SMD]"]
  R1 = Resistor [tolerance=±5% resistance=220 package="2010 [SMD]"]
  R2 = Resistor [tolerance=±5% resistance=220 package="2010 [SMD]"]
  LCM1602_IIC1 = LCM1602 IIC [part_number="LCM1602 IIC" chip_label="LCM1602 IIC" package="DIP (Dual Inline) [THT]"]
  LCD1 = LCD screen
  Microphone = SPW2430
  U1 = POT [knob_status=50% power=0.5W package=pot_mammoth]
  S2 = Pushbutton [package="[SMD]"]
  J1 = Power Jack [package=power_jack_combo]
  S3 = Taiway 100-SP-X-T1 SPDT Miniature Toggle Switch [part_number=100-SP-X-T1-0-0-B1-M1 package=THT]

nets:
  N1: Arduino_Uno.A0, Microphone.AC
  N2: Arduino_Uno.A1, U1.A
  N3: Arduino_Uno.A4/SDA, LCM1602_IIC1.SCL
  N4: Arduino_Uno.A5/SCL, LCM1602_IIC1.SDA
  5V: Arduino_Uno.5V, DRV_1.MS1, LCM1602_IIC1.VCC, U1.S
  N5: Arduino_Uno.ICSP_MOSI, Arduino_Uno.D11_PWM/MOSI, DRV_1.DIRECTION
  N6: Arduino_Uno.D12/MISO, DRV_1.STEP
  N7: Arduino_Uno.D2, S2.Pin_1, S2.Pin_2
  N8: Arduino_Uno.D3_PWM, S1.Pin_1, S1.Pin_2
  N9: Arduino_Uno.D4, R2.Pin_1
  N10: Arduino_Uno.D5_PWM, R1.Pin_1
  N11: Arduino_Uno.D6_PWM, Microphone.DC
  3V3: Arduino_Uno.3V3, Microphone.VIN
  GND: Arduino_Uno.GND, DRV_1.RESET, DRV_1.SLEEP, RED.cathode, GREEN.cathode, S1.Pin_3, S1.Pin_4, LCM1602_IIC1.GND, Microphone.GND, U1.E, S2.Pin_3, S2.Pin_4
  N12: C1.-, DRV_1.GROUND_ST/_MT, J1.GND
  N13: C1.+, DRV_1.VOLTAGE_ST/_MT, J1.PWR
  N14: DRV_1.OUT_2B, M2.A
  N15: DRV_1.OUT_2A, M2.C
  N16: DRV_1.OUT_1A, M2.B
  N17: DRV_1.OUT_1B, M2.D
  N18: RED.anode, R2.Pin_0
  N19: GREEN.anode, R1.Pin_0
  VSS: LCM1602_IIC1.VSS, LCD1.VSS
  VDD: LCM1602_IIC1.VDD, LCD1.VDD
  N20: LCM1602_IIC1.V0, LCD1.V0
  N21: LCM1602_IIC1.RS, LCD1.RS
  N22: LCM1602_IIC1.RW, LCD1.R/W
  N23: LCM1602_IIC1.E, LCD1.E
  N24: LCM1602_IIC1.D0, LCD1.DB0
  N25: LCM1602_IIC1.D1, LCD1.DB1
  N26: LCM1602_IIC1.D2, LCD1.DB2
  N27: LCM1602_IIC1.D3, LCD1.DB3
  N28: LCM1602_IIC1.D4, LCD1.DB4
  N29: LCM1602_IIC1.D5, LCD1.DB5
  N30: LCM1602_IIC1.D6, LCD1.DB6
  N31: LCM1602_IIC1.D7, LCD1.DB7
  N32: LCM1602_IIC1.A, LCD1.LED+
  N33: LCM1602_IIC1.K, LCD1.LED-
  N34: LCM1602_IIC1.LED_A, S3.COM
  N35: LCM1602_IIC1.LED_B, S3.L1

custom parts:
  LCM1602 IIC: I2C-Module to use a 1602 or 2004 LCD on with the wire.h libory Serial LCD Modul
  SPW2430: Just like 'classic' electret microphones, MEMS mics can detect sound and convert it to voltage, but they don't need a bias resistor or amplifier, its all in one! The SPW2430 is a small, low cost MEMS mic with a range of 100Hz - 10KHz, good for just about all general audio recording/detection. This breakout is best used for projects such as voice changers, audio recording/sampling, and audio-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
